// Logisim project maya.circ as structural Verilog: 10 circuits, main circuit main
module main (
  input  [4:0] n
);

  wire [3:0] and_1_out, bit_extender_1_out, creator_1_f0, creator_1_f1, creator_1_f2, creator_1_f3,
       creator_2_f0, creator_2_f1, creator_2_f2, creator_2_f3, creator_4bit_1_f0, creator_4bit_1_f1,
       creator_4bit_1_f2, creator_noai_1_f0, creator_noai_1_f1, creator_noai_1_f2, creator_noai_1_f3,
       eater_rom_1_f0, eater_rom_1_f1, eater_rom_1_f2, eater_rom_1_f3;

  CREATOR creator_1 (.n(n), .F3(creator_1_f3), .F2(creator_1_f2), .F0(creator_1_f0), .F1(creator_1_f1));
  CREATOR creator_2 (.n(n), .F3(creator_2_f3), .F2(creator_2_f2), .F0(creator_2_f0), .F1(creator_2_f1));
  CREATOR_noAI creator_noai_1 (
    .n(n), .F3(creator_noai_1_f3), .F2(creator_noai_1_f2), .F0(creator_noai_1_f0), .F1(creator_noai_1_f1));
  LED led_1 (.in(creator_2_f3[3]));
  LED led_2 (.in(creator_2_f3[3]));
  LED led_3 (.in(creator_2_f3[2]));
  LED led_4 (.in(creator_2_f3[2]));
  LED led_5 (.in(creator_2_f3[2]));
  LED led_6 (.in(creator_2_f3[2]));
  LED led_7 (.in(creator_2_f3[3]));
  LED led_8 (.in(creator_2_f3[3]));
  LED led_9 (.in(creator_2_f2[3]));
  LED led_10 (.in(creator_2_f2[3]));
  LED led_11 (.in(creator_2_f2[2]));
  LED led_12 (.in(creator_2_f2[2]));
  LED led_13 (.in(creator_2_f2[2]));
  LED led_14 (.in(creator_2_f2[2]));
  LED led_15 (.in(creator_2_f2[3]));
  LED led_16 (.in(creator_2_f2[3]));
  LED led_17 (.in(creator_2_f1[3]));
  LED led_18 (.in(creator_2_f1[3]));
  LED led_19 (.in(creator_2_f1[2]));
  LED led_20 (.in(creator_2_f1[2]));
  LED led_21 (.in(creator_2_f1[2]));
  LED led_22 (.in(creator_2_f1[2]));
  LED led_23 (.in(creator_2_f1[3]));
  LED led_24 (.in(creator_2_f1[3]));
  LED led_25 (.in(creator_2_f0[3]));
  LED led_26 (.in(creator_2_f0[3]));
  LED led_27 (.in(creator_2_f0[2]));
  LED led_28 (.in(creator_2_f0[2]));
  LED led_29 (.in(creator_2_f0[2]));
  LED led_30 (.in(creator_2_f0[2]));
  LED led_31 (.in(creator_2_f0[3]));
  LED led_32 (.in(creator_2_f0[3]));
  LED led_33 (.in(creator_noai_1_f3[3]));
  LED led_34 (.in(creator_noai_1_f3[3]));
  LED led_35 (.in(creator_noai_1_f3[2]));
  LED led_36 (.in(creator_noai_1_f3[2]));
  LED led_37 (.in(creator_noai_1_f3[2]));
  LED led_38 (.in(creator_noai_1_f3[2]));
  LED led_39 (.in(creator_noai_1_f3[3]));
  LED led_40 (.in(creator_noai_1_f3[3]));
  LED led_41 (.in(creator_noai_1_f2[3]));
  LED led_42 (.in(creator_noai_1_f2[3]));
  LED led_43 (.in(creator_noai_1_f2[2]));
  LED led_44 (.in(creator_noai_1_f2[2]));
  LED led_45 (.in(creator_noai_1_f2[2]));
  LED led_46 (.in(creator_noai_1_f2[2]));
  LED led_47 (.in(creator_noai_1_f2[3]));
  LED led_48 (.in(creator_noai_1_f2[3]));
  LED led_49 (.in(creator_noai_1_f1[3]));
  LED led_50 (.in(creator_noai_1_f1[3]));
  LED led_51 (.in(creator_noai_1_f1[2]));
  LED led_52 (.in(creator_noai_1_f1[2]));
  LED led_53 (.in(creator_noai_1_f1[2]));
  LED led_54 (.in(creator_noai_1_f1[2]));
  LED led_55 (.in(creator_noai_1_f1[3]));
  LED led_56 (.in(creator_noai_1_f1[3]));
  LED led_57 (.in(creator_noai_1_f0[3]));
  LED led_58 (.in(creator_noai_1_f0[3]));
  LED led_59 (.in(creator_noai_1_f0[2]));
  LED led_60 (.in(creator_noai_1_f0[2]));
  LED led_61 (.in(creator_noai_1_f0[2]));
  LED led_62 (.in(creator_noai_1_f0[2]));
  LED led_63 (.in(creator_noai_1_f0[3]));
  LED led_64 (.in(creator_noai_1_f0[3]));
  LED led_65 (.in(creator_2_f3[1]));
  LED led_66 (.in(creator_2_f3[1]));
  LED led_67 (.in(creator_2_f3[0]));
  LED led_68 (.in(creator_2_f3[0]));
  LED led_69 (.in(creator_2_f3[1]));
  LED led_70 (.in(creator_2_f3[1]));
  LED led_71 (.in(creator_2_f3[0]));
  LED led_72 (.in(creator_2_f3[0]));
  LED led_73 (.in(creator_2_f2[1]));
  LED led_74 (.in(creator_2_f2[1]));
  LED led_75 (.in(creator_2_f2[0]));
  LED led_76 (.in(creator_2_f2[0]));
  LED led_77 (.in(creator_2_f2[1]));
  LED led_78 (.in(creator_2_f2[1]));
  LED led_79 (.in(creator_2_f2[0]));
  LED led_80 (.in(creator_2_f2[0]));
  LED led_81 (.in(creator_2_f1[1]));
  LED led_82 (.in(creator_2_f1[1]));
  LED led_83 (.in(creator_2_f1[0]));
  LED led_84 (.in(creator_2_f1[0]));
  LED led_85 (.in(creator_2_f1[1]));
  LED led_86 (.in(creator_2_f1[1]));
  LED led_87 (.in(creator_2_f1[0]));
  LED led_88 (.in(creator_2_f1[0]));
  LED led_89 (.in(creator_2_f0[1]));
  LED led_90 (.in(creator_2_f0[1]));
  LED led_91 (.in(creator_2_f0[0]));
  LED led_92 (.in(creator_2_f0[0]));
  LED led_93 (.in(creator_2_f0[1]));
  LED led_94 (.in(creator_2_f0[1]));
  LED led_95 (.in(creator_2_f0[0]));
  LED led_96 (.in(creator_2_f0[0]));
  LED led_97 (.in(creator_noai_1_f3[1]));
  LED led_98 (.in(creator_noai_1_f3[1]));
  LED led_99 (.in(creator_noai_1_f3[0]));
  LED led_100 (.in(creator_noai_1_f3[0]));
  LED led_101 (.in(creator_noai_1_f3[1]));
  LED led_102 (.in(creator_noai_1_f3[1]));
  LED led_103 (.in(creator_noai_1_f3[0]));
  LED led_104 (.in(creator_noai_1_f3[0]));
  LED led_105 (.in(creator_noai_1_f2[1]));
  LED led_106 (.in(creator_noai_1_f2[1]));
  LED led_107 (.in(creator_noai_1_f2[0]));
  LED led_108 (.in(creator_noai_1_f2[0]));
  LED led_109 (.in(creator_noai_1_f2[1]));
  LED led_110 (.in(creator_noai_1_f2[1]));
  LED led_111 (.in(creator_noai_1_f2[0]));
  LED led_112 (.in(creator_noai_1_f2[0]));
  LED led_113 (.in(creator_noai_1_f1[1]));
  LED led_114 (.in(creator_noai_1_f1[1]));
  LED led_115 (.in(creator_noai_1_f1[0]));
  LED led_116 (.in(creator_noai_1_f1[0]));
  LED led_117 (.in(creator_noai_1_f1[1]));
  LED led_118 (.in(creator_noai_1_f1[1]));
  LED led_119 (.in(creator_noai_1_f1[0]));
  LED led_120 (.in(creator_noai_1_f1[0]));
  LED led_121 (.in(creator_noai_1_f0[1]));
  LED led_122 (.in(creator_noai_1_f0[1]));
  LED led_123 (.in(creator_noai_1_f0[0]));
  LED led_124 (.in(creator_noai_1_f0[0]));
  LED led_125 (.in(creator_noai_1_f0[1]));
  LED led_126 (.in(creator_noai_1_f0[1]));
  LED led_127 (.in(creator_noai_1_f0[0]));
  LED led_128 (.in(creator_noai_1_f0[0]));
  LED led_129 (.in(creator_2_f3[1]));
  LED led_130 (.in(creator_2_f3[1]));
  LED led_131 (.in(creator_2_f3[2]));
  LED led_132 (.in(creator_2_f3[2]));
  LED led_133 (.in(creator_2_f3[1]));
  LED led_134 (.in(creator_2_f3[1]));
  LED led_135 (.in(creator_2_f3[2]));
  LED led_136 (.in(creator_2_f3[2]));
  LED led_137 (.in(creator_2_f2[1]));
  LED led_138 (.in(creator_2_f2[1]));
  LED led_139 (.in(creator_2_f2[2]));
  LED led_140 (.in(creator_2_f2[2]));
  LED led_141 (.in(creator_2_f2[1]));
  LED led_142 (.in(creator_2_f2[1]));
  LED led_143 (.in(creator_2_f2[2]));
  LED led_144 (.in(creator_2_f2[2]));
  LED led_145 (.in(creator_2_f1[1]));
  LED led_146 (.in(creator_2_f1[1]));
  LED led_147 (.in(creator_2_f1[2]));
  LED led_148 (.in(creator_2_f1[2]));
  LED led_149 (.in(creator_2_f1[1]));
  LED led_150 (.in(creator_2_f1[1]));
  LED led_151 (.in(creator_2_f1[2]));
  LED led_152 (.in(creator_2_f1[2]));
  LED led_153 (.in(creator_2_f0[1]));
  LED led_154 (.in(creator_2_f0[1]));
  LED led_155 (.in(creator_2_f0[2]));
  LED led_156 (.in(creator_2_f0[2]));
  LED led_157 (.in(creator_2_f0[1]));
  LED led_158 (.in(creator_2_f0[1]));
  LED led_159 (.in(creator_2_f0[2]));
  LED led_160 (.in(creator_2_f0[2]));
  LED led_161 (.in(creator_noai_1_f3[1]));
  LED led_162 (.in(creator_noai_1_f3[1]));
  LED led_163 (.in(creator_noai_1_f3[2]));
  LED led_164 (.in(creator_noai_1_f3[2]));
  LED led_165 (.in(creator_noai_1_f3[1]));
  LED led_166 (.in(creator_noai_1_f3[1]));
  LED led_167 (.in(creator_noai_1_f3[2]));
  LED led_168 (.in(creator_noai_1_f3[2]));
  LED led_169 (.in(creator_noai_1_f2[1]));
  LED led_170 (.in(creator_noai_1_f2[1]));
  LED led_171 (.in(creator_noai_1_f2[2]));
  LED led_172 (.in(creator_noai_1_f2[2]));
  LED led_173 (.in(creator_noai_1_f2[1]));
  LED led_174 (.in(creator_noai_1_f2[1]));
  LED led_175 (.in(creator_noai_1_f2[2]));
  LED led_176 (.in(creator_noai_1_f2[2]));
  LED led_177 (.in(creator_noai_1_f1[1]));
  LED led_178 (.in(creator_noai_1_f1[1]));
  LED led_179 (.in(creator_noai_1_f1[2]));
  LED led_180 (.in(creator_noai_1_f1[2]));
  LED led_181 (.in(creator_noai_1_f1[1]));
  LED led_182 (.in(creator_noai_1_f1[1]));
  LED led_183 (.in(creator_noai_1_f1[2]));
  LED led_184 (.in(creator_noai_1_f1[2]));
  LED led_185 (.in(creator_noai_1_f0[1]));
  LED led_186 (.in(creator_noai_1_f0[1]));
  LED led_187 (.in(creator_noai_1_f0[2]));
  LED led_188 (.in(creator_noai_1_f0[2]));
  LED led_189 (.in(creator_noai_1_f0[1]));
  LED led_190 (.in(creator_noai_1_f0[1]));
  LED led_191 (.in(creator_noai_1_f0[2]));
  LED led_192 (.in(creator_noai_1_f0[2]));
  LED led_193 (.in(creator_2_f3[3]));
  LED led_194 (.in(creator_2_f3[3]));
  LED led_195 (.in(creator_2_f3[3]));
  LED led_196 (.in(creator_2_f3[3]));
  LED led_197 (.in(creator_2_f2[3]));
  LED led_198 (.in(creator_2_f2[3]));
  LED led_199 (.in(creator_2_f2[3]));
  LED led_200 (.in(creator_2_f2[3]));
  LED led_201 (.in(creator_2_f1[3]));
  LED led_202 (.in(creator_2_f1[3]));
  LED led_203 (.in(creator_2_f1[3]));
  LED led_204 (.in(creator_2_f1[3]));
  LED led_205 (.in(creator_2_f0[3]));
  LED led_206 (.in(creator_2_f0[3]));
  LED led_207 (.in(creator_2_f0[3]));
  LED led_208 (.in(creator_2_f0[3]));
  LED led_209 (.in(creator_noai_1_f3[3]));
  LED led_210 (.in(creator_noai_1_f3[3]));
  LED led_211 (.in(creator_noai_1_f3[3]));
  LED led_212 (.in(creator_noai_1_f3[3]));
  LED led_213 (.in(creator_noai_1_f2[3]));
  LED led_214 (.in(creator_noai_1_f2[3]));
  LED led_215 (.in(creator_noai_1_f2[3]));
  LED led_216 (.in(creator_noai_1_f2[3]));
  LED led_217 (.in(creator_noai_1_f1[3]));
  LED led_218 (.in(creator_noai_1_f1[3]));
  LED led_219 (.in(creator_noai_1_f1[3]));
  LED led_220 (.in(creator_noai_1_f1[3]));
  LED led_221 (.in(creator_noai_1_f0[3]));
  LED led_222 (.in(creator_noai_1_f0[3]));
  LED led_223 (.in(creator_noai_1_f0[3]));
  LED led_224 (.in(creator_noai_1_f0[3]));
  EATER_ROM eater_rom_1 (.n(n), .F3(eater_rom_1_f3), .F2(eater_rom_1_f2), .F0(eater_rom_1_f0), .F1(eater_rom_1_f1));
  CREATOR_4bit creator_4bit_1 (.n(and_1_out), .F2(creator_4bit_1_f2), .F0(creator_4bit_1_f0), .F1(creator_4bit_1_f1));
  LED led_225 (.in(eater_rom_1_f3[3]));
  LED led_226 (.in(eater_rom_1_f3[3]));
  LED led_227 (.in(eater_rom_1_f3[3]));
  LED led_228 (.in(eater_rom_1_f3[3]));
  LED led_229 (.in(eater_rom_1_f2[3]));
  LED led_230 (.in(eater_rom_1_f2[3]));
  LED led_231 (.in(eater_rom_1_f2[3]));
  LED led_232 (.in(eater_rom_1_f2[3]));
  LED led_233 (.in(eater_rom_1_f1[3]));
  LED led_234 (.in(eater_rom_1_f1[3]));
  LED led_235 (.in(eater_rom_1_f1[3]));
  LED led_236 (.in(eater_rom_1_f1[3]));
  LED led_237 (.in(eater_rom_1_f0[3]));
  LED led_238 (.in(eater_rom_1_f0[3]));
  LED led_239 (.in(eater_rom_1_f0[3]));
  LED led_240 (.in(eater_rom_1_f0[3]));
  assign bit_extender_1_out = {{3{n[4]}}, n[4]};  // Bit_Extender bit_extender_1
  assign and_1_out = ~bit_extender_1_out & n[3:0];  // AND_Gate and_1, 4 bits wide
  LED led_241 (.in(creator_4bit_1_f2[3]));
  LED led_242 (.in(creator_4bit_1_f2[3]));
  LED led_243 (.in(creator_4bit_1_f2[3]));
  LED led_244 (.in(creator_4bit_1_f2[3]));
  LED led_245 (.in(creator_4bit_1_f1[3]));
  LED led_246 (.in(creator_4bit_1_f1[3]));
  LED led_247 (.in(creator_4bit_1_f1[3]));
  LED led_248 (.in(creator_4bit_1_f1[3]));
  LED led_249 (.in(creator_4bit_1_f0[3]));
  LED led_250 (.in(creator_4bit_1_f0[3]));
  LED led_251 (.in(creator_4bit_1_f0[3]));
  LED led_252 (.in(creator_4bit_1_f0[3]));
  LED led_253 (.in(eater_rom_1_f3[2]));
  LED led_254 (.in(eater_rom_1_f3[2]));
  LED led_255 (.in(eater_rom_1_f3[1]));
  LED led_256 (.in(eater_rom_1_f3[1]));
  LED led_257 (.in(eater_rom_1_f3[2]));
  LED led_258 (.in(eater_rom_1_f3[2]));
  LED led_259 (.in(eater_rom_1_f3[1]));
  LED led_260 (.in(eater_rom_1_f3[1]));
  LED led_261 (.in(eater_rom_1_f2[2]));
  LED led_262 (.in(eater_rom_1_f2[2]));
  LED led_263 (.in(eater_rom_1_f2[1]));
  LED led_264 (.in(eater_rom_1_f2[1]));
  LED led_265 (.in(eater_rom_1_f2[2]));
  LED led_266 (.in(eater_rom_1_f2[2]));
  LED led_267 (.in(eater_rom_1_f2[1]));
  LED led_268 (.in(eater_rom_1_f2[1]));
  LED led_269 (.in(eater_rom_1_f1[2]));
  LED led_270 (.in(eater_rom_1_f1[2]));
  LED led_271 (.in(eater_rom_1_f1[1]));
  LED led_272 (.in(eater_rom_1_f1[1]));
  LED led_273 (.in(eater_rom_1_f1[2]));
  LED led_274 (.in(eater_rom_1_f1[2]));
  LED led_275 (.in(eater_rom_1_f1[1]));
  LED led_276 (.in(eater_rom_1_f1[1]));
  LED led_277 (.in(eater_rom_1_f0[2]));
  LED led_278 (.in(eater_rom_1_f0[2]));
  LED led_279 (.in(eater_rom_1_f0[1]));
  LED led_280 (.in(eater_rom_1_f0[1]));
  LED led_281 (.in(eater_rom_1_f0[2]));
  LED led_282 (.in(eater_rom_1_f0[2]));
  LED led_283 (.in(eater_rom_1_f0[1]));
  LED led_284 (.in(eater_rom_1_f0[1]));
  LED led_285 (.in(creator_4bit_1_f2[2]));
  LED led_286 (.in(creator_4bit_1_f2[2]));
  LED led_287 (.in(creator_4bit_1_f2[1]));
  LED led_288 (.in(creator_4bit_1_f2[1]));
  LED led_289 (.in(creator_4bit_1_f2[2]));
  LED led_290 (.in(creator_4bit_1_f2[2]));
  LED led_291 (.in(creator_4bit_1_f2[1]));
  LED led_292 (.in(creator_4bit_1_f2[1]));
  LED led_293 (.in(creator_4bit_1_f1[2]));
  LED led_294 (.in(creator_4bit_1_f1[2]));
  LED led_295 (.in(creator_4bit_1_f1[1]));
  LED led_296 (.in(creator_4bit_1_f1[1]));
  LED led_297 (.in(creator_4bit_1_f1[2]));
  LED led_298 (.in(creator_4bit_1_f1[2]));
  LED led_299 (.in(creator_4bit_1_f1[1]));
  LED led_300 (.in(creator_4bit_1_f1[1]));
  LED led_301 (.in(creator_4bit_1_f0[2]));
  LED led_302 (.in(creator_4bit_1_f0[2]));
  LED led_303 (.in(creator_4bit_1_f0[1]));
  LED led_304 (.in(creator_4bit_1_f0[1]));
  LED led_305 (.in(creator_4bit_1_f0[2]));
  LED led_306 (.in(creator_4bit_1_f0[2]));
  LED led_307 (.in(creator_4bit_1_f0[1]));
  LED led_308 (.in(creator_4bit_1_f0[1]));
  LED led_309 (.in(eater_rom_1_f3[0]));
  LED led_310 (.in(eater_rom_1_f3[0]));
  LED led_311 (.in(eater_rom_1_f3[1]));
  LED led_312 (.in(eater_rom_1_f3[1]));
  LED led_313 (.in(eater_rom_1_f3[0]));
  LED led_314 (.in(eater_rom_1_f3[0]));
  LED led_315 (.in(eater_rom_1_f3[1]));
  LED led_316 (.in(eater_rom_1_f3[1]));
  LED led_317 (.in(eater_rom_1_f2[0]));
  LED led_318 (.in(eater_rom_1_f2[0]));
  LED led_319 (.in(eater_rom_1_f2[1]));
  LED led_320 (.in(eater_rom_1_f2[1]));
  LED led_321 (.in(eater_rom_1_f2[0]));
  LED led_322 (.in(eater_rom_1_f2[0]));
  LED led_323 (.in(eater_rom_1_f2[1]));
  LED led_324 (.in(eater_rom_1_f2[1]));
  LED led_325 (.in(eater_rom_1_f1[0]));
  LED led_326 (.in(eater_rom_1_f1[0]));
  LED led_327 (.in(eater_rom_1_f1[1]));
  LED led_328 (.in(eater_rom_1_f1[1]));
  LED led_329 (.in(eater_rom_1_f1[0]));
  LED led_330 (.in(eater_rom_1_f1[0]));
  LED led_331 (.in(eater_rom_1_f1[1]));
  LED led_332 (.in(eater_rom_1_f1[1]));
  LED led_333 (.in(eater_rom_1_f0[0]));
  LED led_334 (.in(eater_rom_1_f0[0]));
  LED led_335 (.in(eater_rom_1_f0[1]));
  LED led_336 (.in(eater_rom_1_f0[1]));
  LED led_337 (.in(eater_rom_1_f0[0]));
  LED led_338 (.in(eater_rom_1_f0[0]));
  LED led_339 (.in(eater_rom_1_f0[1]));
  LED led_340 (.in(eater_rom_1_f0[1]));
  LED led_341 (.in(creator_4bit_1_f2[0]));
  LED led_342 (.in(creator_4bit_1_f2[0]));
  LED led_343 (.in(creator_4bit_1_f2[1]));
  LED led_344 (.in(creator_4bit_1_f2[1]));
  LED led_345 (.in(creator_4bit_1_f2[0]));
  LED led_346 (.in(creator_4bit_1_f2[0]));
  LED led_347 (.in(creator_4bit_1_f2[1]));
  LED led_348 (.in(creator_4bit_1_f2[1]));
  LED led_349 (.in(creator_4bit_1_f1[0]));
  LED led_350 (.in(creator_4bit_1_f1[0]));
  LED led_351 (.in(creator_4bit_1_f1[1]));
  LED led_352 (.in(creator_4bit_1_f1[1]));
  LED led_353 (.in(creator_4bit_1_f1[0]));
  LED led_354 (.in(creator_4bit_1_f1[0]));
  LED led_355 (.in(creator_4bit_1_f1[1]));
  LED led_356 (.in(creator_4bit_1_f1[1]));
  LED led_357 (.in(creator_4bit_1_f0[0]));
  LED led_358 (.in(creator_4bit_1_f0[0]));
  LED led_359 (.in(creator_4bit_1_f0[1]));
  LED led_360 (.in(creator_4bit_1_f0[1]));
  LED led_361 (.in(creator_4bit_1_f0[0]));
  LED led_362 (.in(creator_4bit_1_f0[0]));
  LED led_363 (.in(creator_4bit_1_f0[1]));
  LED led_364 (.in(creator_4bit_1_f0[1]));
  LED led_365 (.in(eater_rom_1_f3[2]));
  LED led_366 (.in(eater_rom_1_f3[2]));
  LED led_367 (.in(eater_rom_1_f3[3]));
  LED led_368 (.in(eater_rom_1_f3[3]));
  LED led_369 (.in(eater_rom_1_f3[2]));
  LED led_370 (.in(eater_rom_1_f3[2]));
  LED led_371 (.in(eater_rom_1_f3[3]));
  LED led_372 (.in(eater_rom_1_f3[3]));
  LED led_373 (.in(eater_rom_1_f2[2]));
  LED led_374 (.in(eater_rom_1_f2[2]));
  LED led_375 (.in(eater_rom_1_f2[3]));
  LED led_376 (.in(eater_rom_1_f2[3]));
  LED led_377 (.in(eater_rom_1_f2[2]));
  LED led_378 (.in(eater_rom_1_f2[2]));
  LED led_379 (.in(eater_rom_1_f2[3]));
  LED led_380 (.in(eater_rom_1_f2[3]));
  LED led_381 (.in(eater_rom_1_f1[2]));
  LED led_382 (.in(eater_rom_1_f1[2]));
  LED led_383 (.in(eater_rom_1_f1[3]));
  LED led_384 (.in(eater_rom_1_f1[3]));
  LED led_385 (.in(eater_rom_1_f1[2]));
  LED led_386 (.in(eater_rom_1_f1[2]));
  LED led_387 (.in(eater_rom_1_f1[3]));
  LED led_388 (.in(eater_rom_1_f1[3]));
  LED led_389 (.in(eater_rom_1_f0[2]));
  LED led_390 (.in(eater_rom_1_f0[2]));
  LED led_391 (.in(eater_rom_1_f0[3]));
  LED led_392 (.in(eater_rom_1_f0[3]));
  LED led_393 (.in(eater_rom_1_f0[2]));
  LED led_394 (.in(eater_rom_1_f0[2]));
  LED led_395 (.in(eater_rom_1_f0[3]));
  LED led_396 (.in(eater_rom_1_f0[3]));
  LED led_397 (.in(creator_4bit_1_f2[2]));
  LED led_398 (.in(creator_4bit_1_f2[2]));
  LED led_399 (.in(creator_4bit_1_f2[3]));
  LED led_400 (.in(creator_4bit_1_f2[3]));
  LED led_401 (.in(creator_4bit_1_f2[2]));
  LED led_402 (.in(creator_4bit_1_f2[2]));
  LED led_403 (.in(creator_4bit_1_f2[3]));
  LED led_404 (.in(creator_4bit_1_f2[3]));
  LED led_405 (.in(creator_4bit_1_f1[2]));
  LED led_406 (.in(creator_4bit_1_f1[2]));
  LED led_407 (.in(creator_4bit_1_f1[3]));
  LED led_408 (.in(creator_4bit_1_f1[3]));
  LED led_409 (.in(creator_4bit_1_f1[2]));
  LED led_410 (.in(creator_4bit_1_f1[2]));
  LED led_411 (.in(creator_4bit_1_f1[3]));
  LED led_412 (.in(creator_4bit_1_f1[3]));
  LED led_413 (.in(creator_4bit_1_f0[2]));
  LED led_414 (.in(creator_4bit_1_f0[2]));
  LED led_415 (.in(creator_4bit_1_f0[3]));
  LED led_416 (.in(creator_4bit_1_f0[3]));
  LED led_417 (.in(creator_4bit_1_f0[2]));
  LED led_418 (.in(creator_4bit_1_f0[2]));
  LED led_419 (.in(creator_4bit_1_f0[3]));
  LED led_420 (.in(creator_4bit_1_f0[3]));

  // Notes on the sheet:
  //   Wiring
  //   CREATOR
  //   No AI
  //   Showcase
  //   ROM
  //   4 bits
endmodule

module EATER (
  input  [4:0] n,
  output C0,
  output C1,
  output C2,
  output R0,
  output R1
);

  wire and_1_out, and_2_out, and_3_out, and_4_out, and_5_out, and_6_out, and_7_out, and_8_out, and_9_out,
       and_10_out, and_11_out, or_2_out, or_4_out, or_7_out, variables_1_a, variables_1_b, variables_1_c,
       variables_1_d, variables_1_e, variables_1_f, variables_1_g, variables_1_y0, variables_1_y1,
       variables_1_y2, xor_1_out, xor_2_out, xor_3_out, xor_4_out;

  VARIABLES variables_1 (
    .n(n), .y0(variables_1_y0), .y1(variables_1_y1), .y2(variables_1_y2), .a(variables_1_a),
    .b(variables_1_b), .c(variables_1_c), .d(variables_1_d), .e(variables_1_e), .f(variables_1_f),
    .g(variables_1_g));
  and and_1 (and_1_out, variables_1_g, variables_1_f);
  or or_1 (R1, variables_1_d, and_1_out);
  and and_2 (and_2_out, variables_1_g, ~variables_1_f);  // AND_Gate
  or or_2 (or_2_out, variables_1_b, ~n[3]);  // OR_Gate
  or or_3 (R0, and_2_out, variables_1_d, and_4_out);
  or or_4 (or_4_out, n[1], n[0]);
  and and_3 (and_3_out, variables_1_e, ~variables_1_y1, ~n[0]);  // AND_Gate
  and and_4 (and_4_out, or_2_out, variables_1_e, or_4_out);
  xor xor_1 (xor_1_out, n[4], n[3]);
  and and_5 (and_5_out, ~n[2], n[0]);  // AND_Gate
  and and_6 (and_6_out, xor_1_out, variables_1_y1, and_5_out);
  or or_5 (C2, and_3_out, and_6_out);
  xor xor_2 (xor_2_out, n[1], n[0]);
  and and_7 (and_7_out, variables_1_d, xor_2_out);
  and and_8 (and_8_out, variables_1_a, or_7_out);
  or or_6 (C1, and_7_out, and_8_out);
  or or_7 (or_7_out, ~variables_1_y2, variables_1_y0);  // OR_Gate
  xor xor_3 (xor_3_out, n[4], n[0]);
  and and_9 (and_9_out, xor_3_out, ~variables_1_c);  // AND_Gate
  and and_10 (and_10_out, variables_1_b, ~n[4], ~n[2]);  // AND_Gate
  xor xor_4 (xor_4_out, variables_1_y0, n[2]);
  and and_11 (and_11_out, variables_1_a, xor_4_out);
  or or_8 (C0, and_9_out, and_10_out, and_11_out);

  // Notes on the sheet:
  //   x0
  //   x1
  //   x2
  //   x3
  //   x4
  //   R1
  //   R0
  //   C2
  //   C1
  //   C0
endmodule

module EATER_noAI (
  input  [4:0] n,
  output C0,
  output C1,
  output C2,
  output R0,
  output R1
);

  wire and_1_out, and_2_out, and_3_out, and_4_out, and_5_out, and_6_out, and_7_out, and_8_out, and_9_out,
       and_10_out, and_11_out, and_12_out, and_13_out, and_14_out, and_15_out, and_16_out, and_17_out,
       and_18_out, and_19_out, and_20_out, and_21_out, and_22_out, and_23_out, and_24_out, and_25_out,
       and_26_out, and_27_out, and_28_out, nor_1_out, nor_2_out, nor_3_out, nor_4_out, nor_5_out, nor_6_out,
       or_1_out, or_3_out, or_5_out, or_6_out, or_8_out, or_9_out, or_11_out, or_12_out, xor_1_out, xor_2_out;

  and and_1 (and_1_out, n[4], ~n[3], ~n[2]);  // AND_Gate
  and and_2 (and_2_out, ~n[4], n[3]);  // AND_Gate
  or or_1 (or_1_out, n[2], n[1]);
  and and_3 (and_3_out, and_2_out, or_1_out);
  or or_2 (R1, and_1_out, and_3_out);
  and and_4 (and_4_out, n[4], ~n[3], ~n[2]);  // AND_Gate
  and and_5 (and_5_out, ~n[4], n[3]);  // AND_Gate
  and and_6 (and_6_out, n[2], n[1], n[0]);
  nor nor_1 (nor_1_out, n[2], n[1]);
  nor nor_2 (nor_2_out, n[4], n[3]);
  or or_3 (or_3_out, nor_1_out, and_6_out);
  and and_7 (and_7_out, and_5_out, or_3_out);
  or or_4 (R0, and_4_out, and_7_out, and_9_out);
  or or_5 (or_5_out, n[1], n[0]);
  and and_8 (and_8_out, n[2], or_5_out);
  and and_9 (and_9_out, nor_2_out, and_8_out);
  and and_10 (and_10_out, ~n[2], n[0]);  // AND_Gate
  and and_11 (and_11_out, n[4], ~n[3], n[1]);  // AND_Gate
  and and_12 (and_12_out, ~n[4], n[3], ~n[1]);  // AND_Gate
  or or_6 (or_6_out, and_11_out, and_12_out);
  and and_13 (and_13_out, and_10_out, or_6_out);
  or or_7 (C2, and_13_out, and_16_out);
  and and_14 (and_14_out, ~n[4], n[2], ~n[0]);  // AND_Gate
  and and_15 (and_15_out, n[3], n[1]);
  nor nor_3 (nor_3_out, n[3], n[1]);
  or or_8 (or_8_out, and_15_out, nor_3_out);
  and and_16 (and_16_out, and_14_out, or_8_out);
  and and_17 (and_17_out, ~n[4], ~n[3], n[1], n[0]);  // AND_Gate
  and and_18 (and_18_out, n[4], ~n[1], n[0]);  // AND_Gate
  and and_19 (and_19_out, n[1], ~n[0]);  // AND_Gate
  nor nor_4 (nor_4_out, n[3], n[2]);
  or or_9 (or_9_out, and_18_out, and_19_out);
  and and_20 (and_20_out, nor_4_out, or_9_out);
  or or_10 (C1, and_17_out, and_20_out, and_22_out);
  or or_11 (or_11_out, n[2], ~n[0]);  // OR_Gate
  and and_21 (and_21_out, ~n[4], n[3], ~n[1]);  // AND_Gate
  and and_22 (and_22_out, or_11_out, and_21_out);
  xor xor_1 (xor_1_out, n[4], n[0]);
  nor nor_5 (nor_5_out, n[3], n[2]);
  and and_23 (and_23_out, xor_1_out, nor_5_out);
  and and_24 (and_24_out, n[3], ~n[2], ~n[1]);  // AND_Gate
  and and_25 (and_25_out, ~n[3], n[2], n[1]);  // AND_Gate
  nor nor_6 (nor_6_out, n[4], n[0]);
  or or_12 (or_12_out, and_24_out, and_25_out);
  and and_26 (and_26_out, nor_6_out, or_12_out);
  or or_13 (C0, and_23_out, and_26_out, and_28_out);
  and and_27 (and_27_out, ~n[4], n[3], n[0]);  // AND_Gate
  xor xor_2 (xor_2_out, n[2], n[1]);
  and and_28 (and_28_out, and_27_out, xor_2_out);

  // Notes on the sheet:
  //   R1
  //   R0
  //   C2
  //   C1
  //   C0
endmodule

module EATER_4bit (
  input  [3:0] n,
  output C0,
  output C1,
  output C2,
  output R0,
  output R1
);

  wire and_2_out, and_3_out, and_4_out, and_6_out, and_7_out, and_8_out, or_1_out, or_2_out, or_5_out,
       variables_4_1_b, variables_4_1_f, variables_4_1_h, variables_4_1_y0, variables_4_1_y1,
       variables_4_1_y2, xor_1_out;

  VARIABLES_4 variables_4_1 (
    .n(n), .y0(variables_4_1_y0), .y1(variables_4_1_y1), .y2(variables_4_1_y2), .b(variables_4_1_b),
    .f(variables_4_1_f), .h(variables_4_1_h));
  and and_1 (R1, variables_4_1_f, n[3]);
  or or_1 (or_1_out, variables_4_1_b, ~n[3]);  // OR_Gate
  or or_2 (or_2_out, n[1], n[0]);
  and and_2 (and_2_out, or_1_out, n[2], or_2_out);
  or or_3 (R0, variables_4_1_h, and_2_out);
  and and_3 (and_3_out, variables_4_1_h, n[0]);
  and and_4 (and_4_out, ~variables_4_1_y1, n[2], ~n[0]);  // AND_Gate
  or or_4 (C2, and_3_out, and_4_out);
  or or_5 (or_5_out, ~variables_4_1_y2, variables_4_1_y0);  // OR_Gate
  and and_5 (C1, variables_4_1_y1, or_5_out);
  and and_6 (and_6_out, ~variables_4_1_f, variables_4_1_y0);  // AND_Gate
  and and_7 (and_7_out, variables_4_1_b, ~n[2]);  // AND_Gate
  or or_6 (C0, and_6_out, and_7_out, and_8_out);
  xor xor_1 (xor_1_out, n[2], variables_4_1_y0);
  and and_8 (and_8_out, variables_4_1_y1, xor_1_out);

  // Notes on the sheet:
  //   x0
  //   x1
  //   x2
  //   x3
  //   R1
  //   R0
  //   C2
  //   C1
  //   C0
endmodule

module EATER_ROM (
  input  [4:0] n,
  output [3:0] F3,
  output [3:0] F2,
  output [3:0] F0,
  output [3:0] F1
);

  ROM #(.addrWidth(5), .dataWidth(16)) rom_1 (.addr(n), .data({F3, F2, F1, F0}));

  // Notes on the sheet:
  //   contents of rom_1 (hex, n*v repeats v):
  //   787 1 2 5 a f 1f 2f 5f af ff 1ff 2ff 5ff aff fff 1fff 2fff 5fff afff 787 787 787 787 787 787 787 787
  //   787 787 787 787
endmodule

module VARIABLES (
  input  [4:0] n,
  output y0,
  output y1,
  output y2,
  output a,
  output b,
  output c,
  output d,
  output e,
  output f,
  output g
);

  xor xor_1 (y0, n[0], n[3]);
  xor xor_2 (y1, n[1], n[3]);
  xor xor_3 (y2, n[2], n[3]);
  and and_1 (a, y1, ~n[4]);  // AND_Gate
  and and_2 (b, n[0], n[1]);
  or or_1 (c, n[2], n[3]);
  and and_3 (d, ~c, n[4]);  // AND_Gate
  and and_4 (e, n[2], ~n[4]);  // AND_Gate
  or or_2 (f, n[1], n[2]);
  and and_5 (g, n[3], ~n[4]);  // AND_Gate
endmodule

module VARIABLES_4 (
  input  [3:0] n,
  output y0,
  output y1,
  output y2,
  output b,
  output f,
  output h
);

  xor xor_1 (y0, n[0], n[3]);
  xor xor_2 (y1, n[1], n[3]);
  xor xor_3 (y2, n[2], n[3]);
  and and_1 (b, n[0], n[1]);
  or or_1 (f, n[1], n[2]);
  and and_2 (h, ~f, n[3]);  // AND_Gate
endmodule

module CREATOR (
  input  [4:0] n,
  output [3:0] F3,
  output [3:0] F2,
  output [3:0] F0,
  output [3:0] F1
);

  wire and_1_out, and_3_out, eater_1_c1, eater_1_r0, eater_1_r1, nor_1_out, or_1_out;
  wire [3:0] and_7_out, and_8_out, bit_extender_1_out, bit_extender_2_out, bit_extender_3_out, eater_1_c0,
       or_4_out, or_5_out;
  wire [3:2] and_5_out;

  EATER eater_1 (.n(n), .C0(eater_1_c0[0]), .C1(eater_1_c1), .C2(eater_1_c0[3]), .R0(eater_1_r0), .R1(eater_1_r1));
  nor nor_1 (nor_1_out, eater_1_r1, eater_1_r0, eater_1_c0[3], eater_1_c1, eater_1_c0[0]);
  and and_1 (and_1_out, ~eater_1_c0[0], eater_1_c1);  // AND_Gate
  and and_2 (eater_1_c0[2], eater_1_c0[0], eater_1_c1);
  and and_3 (and_3_out, eater_1_r0, eater_1_r1);
  or or_1 (or_1_out, eater_1_r0, eater_1_r1);
  and and_4 (and_5_out[3], nor_1_out, 1'b1);
  and and_5 (and_5_out[2], nor_1_out, 1'b0);
  or or_2 (eater_1_c0[1], and_1_out, eater_1_c0[3]);
  assign bit_extender_1_out = {{3{and_3_out}}, and_3_out};  // Bit_Extender bit_extender_1
  assign bit_extender_2_out = {{3{eater_1_r1}}, eater_1_r1};  // Bit_Extender bit_extender_2
  assign bit_extender_3_out = {{3{or_1_out}}, or_1_out};  // Bit_Extender bit_extender_3
  assign F2 = {and_5_out[2], {3{and_5_out[3]}}} | and_7_out;  // OR_Gate or_3, 4 bits wide
  assign F3 = bit_extender_1_out & eater_1_c0;  // AND_Gate and_6, 4 bits wide
  assign and_7_out = bit_extender_2_out & or_4_out;  // AND_Gate and_7, 4 bits wide
  assign or_4_out = bit_extender_1_out | eater_1_c0;  // OR_Gate or_4, 4 bits wide
  assign or_5_out = bit_extender_2_out | eater_1_c0;  // OR_Gate or_5, 4 bits wide
  assign F0 = {and_5_out[2], {3{and_5_out[3]}}} | bit_extender_3_out | eater_1_c0;  // OR_Gate or_6, 4 bits wide
  assign and_8_out = bit_extender_3_out & or_5_out;  // AND_Gate and_8, 4 bits wide
  assign F1 = {and_5_out, {2{and_5_out[2]}}} | and_8_out;  // OR_Gate or_7, 4 bits wide

  // Notes on the sheet:
  //   EATER
endmodule

module CREATOR_noAI (
  input  [4:0] n,
  output [3:0] F3,
  output [3:0] F2,
  output [3:0] F0,
  output [3:0] F1
);

  wire and_1_out, and_3_out, eater_noai_1_c1, eater_noai_1_r0, eater_noai_1_r1, nor_1_out, or_1_out;
  wire [3:0] and_7_out, and_8_out, bit_extender_1_out, bit_extender_2_out, bit_extender_3_out,
       eater_noai_1_c0, or_4_out, or_5_out;
  wire [3:2] and_5_out;

  EATER_noAI eater_noai_1 (
    .n(n), .C0(eater_noai_1_c0[0]), .C1(eater_noai_1_c1), .C2(eater_noai_1_c0[3]), .R0(eater_noai_1_r0),
    .R1(eater_noai_1_r1));
  nor nor_1 (nor_1_out, eater_noai_1_r1, eater_noai_1_r0, eater_noai_1_c0[3], eater_noai_1_c1, eater_noai_1_c0[0]);
  and and_1 (and_1_out, ~eater_noai_1_c0[0], eater_noai_1_c1);  // AND_Gate
  and and_2 (eater_noai_1_c0[2], eater_noai_1_c0[0], eater_noai_1_c1);
  and and_3 (and_3_out, eater_noai_1_r0, eater_noai_1_r1);
  or or_1 (or_1_out, eater_noai_1_r0, eater_noai_1_r1);
  and and_4 (and_5_out[3], nor_1_out, 1'b1);
  and and_5 (and_5_out[2], nor_1_out, 1'b0);
  or or_2 (eater_noai_1_c0[1], and_1_out, eater_noai_1_c0[3]);
  assign bit_extender_1_out = {{3{and_3_out}}, and_3_out};  // Bit_Extender bit_extender_1
  assign bit_extender_2_out = {{3{eater_noai_1_r1}}, eater_noai_1_r1};  // Bit_Extender bit_extender_2
  assign bit_extender_3_out = {{3{or_1_out}}, or_1_out};  // Bit_Extender bit_extender_3
  assign F2 = {and_5_out[2], {3{and_5_out[3]}}} | and_7_out;  // OR_Gate or_3, 4 bits wide
  assign F3 = bit_extender_1_out & eater_noai_1_c0;  // AND_Gate and_6, 4 bits wide
  assign and_7_out = bit_extender_2_out & or_4_out;  // AND_Gate and_7, 4 bits wide
  assign or_4_out = bit_extender_1_out | eater_noai_1_c0;  // OR_Gate or_4, 4 bits wide
  assign or_5_out = bit_extender_2_out | eater_noai_1_c0;  // OR_Gate or_5, 4 bits wide
  assign F0 = {and_5_out[2], {3{and_5_out[3]}}} | bit_extender_3_out | eater_noai_1_c0;  // OR_Gate or_6, 4 bits wide
  assign and_8_out = bit_extender_3_out & or_5_out;  // AND_Gate and_8, 4 bits wide
  assign F1 = {and_5_out, {2{and_5_out[2]}}} | and_8_out;  // OR_Gate or_7, 4 bits wide

  // Notes on the sheet:
  //   EATER no AI
endmodule

module CREATOR_4bit (
  input  [3:0] n,
  output [3:0] F2,
  output [3:0] F0,
  output [3:0] F1
);

  wire and_1_out, and_3_out, eater_4bit_1_c1, eater_4bit_1_r0, eater_4bit_1_r1, nor_1_out, or_1_out;
  wire [3:0] and_6_out, and_7_out, bit_extender_1_out, bit_extender_2_out, bit_extender_3_out,
       eater_4bit_1_c0, or_4_out, or_5_out;
  wire [3:2] and_5_out;

  EATER_4bit eater_4bit_1 (
    .n(n), .C0(eater_4bit_1_c0[0]), .C1(eater_4bit_1_c1), .C2(eater_4bit_1_c0[3]), .R0(eater_4bit_1_r0),
    .R1(eater_4bit_1_r1));
  nor nor_1 (nor_1_out, eater_4bit_1_r1, eater_4bit_1_r0, eater_4bit_1_c0[3], eater_4bit_1_c1, eater_4bit_1_c0[0]);
  and and_1 (and_1_out, ~eater_4bit_1_c0[0], eater_4bit_1_c1);  // AND_Gate
  and and_2 (eater_4bit_1_c0[2], eater_4bit_1_c0[0], eater_4bit_1_c1);
  and and_3 (and_3_out, eater_4bit_1_r0, eater_4bit_1_r1);
  or or_1 (or_1_out, eater_4bit_1_r0, eater_4bit_1_r1);
  and and_4 (and_5_out[3], nor_1_out, 1'b1);
  and and_5 (and_5_out[2], nor_1_out, 1'b0);
  or or_2 (eater_4bit_1_c0[1], and_1_out, eater_4bit_1_c0[3]);
  assign bit_extender_1_out = {{3{and_3_out}}, and_3_out};  // Bit_Extender bit_extender_1
  assign bit_extender_2_out = {{3{eater_4bit_1_r1}}, eater_4bit_1_r1};  // Bit_Extender bit_extender_2
  assign bit_extender_3_out = {{3{or_1_out}}, or_1_out};  // Bit_Extender bit_extender_3
  assign F2 = {and_5_out[2], {3{and_5_out[3]}}} | and_6_out;  // OR_Gate or_3, 4 bits wide
  assign and_6_out = bit_extender_2_out & or_4_out;  // AND_Gate and_6, 4 bits wide
  assign or_4_out = bit_extender_1_out | eater_4bit_1_c0;  // OR_Gate or_4, 4 bits wide
  assign or_5_out = bit_extender_2_out | eater_4bit_1_c0;  // OR_Gate or_5, 4 bits wide
  assign F0 = {and_5_out[2], {3{and_5_out[3]}}} | bit_extender_3_out | eater_4bit_1_c0;  // OR_Gate or_6, 4 bits wide
  assign and_7_out = bit_extender_3_out & or_5_out;  // AND_Gate and_7, 4 bits wide
  assign F1 = {and_5_out, {2{and_5_out[2]}}} | and_7_out;  // OR_Gate or_7, 4 bits wide

  // Notes on the sheet:
  //   EATER 4 bits
endmodule
